# Fritzing sketch obstacle-sensor (saved by Fritzing 0.9.2b)
breadboards: 1

parts:
  LED1 = LED - 5mm [color="Red (633nm)" package="5 mm [THT]"]
  Componente1 = Arduino Nano (Rev3.0)
  J1 = Piezo Speaker  # not connected
  Componente2 = SRF05 Ultrasonic Rangefinder
  LED2 = smd LED [color="Green (555nm)" package="0603 [SMD]"]

nets:
  GND: LED1.cathode, Componente1.GND, Componente2.GND, LED2.cathode
  N1: LED1.anode, Componente1.A3
  N2: Componente1.D2, Componente2.Trig
  N3: Componente1.D3, Componente2.Echo
  5V: Componente1.5V, Componente2.VCC
  N4: Componente1.A0, LED2.anode
